# Fritzing sketch schematics (saved by Fritzing 0.9.4)
breadboards: 1

parts:
  U2 = ESP32S-HiLetgo [part_number=ESP32S-HiLetgo]
  VCC1 = 4 x AAA Battery Mount
  U3 = L9110 H-bridge module [part_number="L9110 H-bridge"]
  M1 = DC Motor
  M2 = DC Motor
  M3 = DC Motor
  M4 = DC Motor

nets:
  N1: U2.EN, U2.GPIO8
  VIN: U2.GPIO36, U2.GPIO39, U2.GPIO10, U2.VIN, U2.GPIO6, U2.GPIO2, U2.GPIO16, VCC1.-, U3.GND
  N2: U2.GPIO35, U2.GPIO33, U2.GPIO13, VCC1.+, U3.VCC
  N3: U2.GPIO17, U3.A-IB
  N4: U2.GPIO22, U3.B-IA
  N5: U3.MOTOR_A-A, M1.pin_1, M2.pin_1
  N6: U3.MOTOR_A-B, M1.pin_2
  N7: U3.MOTOR_B-A, M3.pin_1, M4.pin_1
  N8: U3.MOTOR_B-B, M3.pin_2, M4.pin_2

notes:
  There should be 6xAAA battery pack

custom parts:
  ESP32S-HiLetgo: HiLetgo ESP-WROOM-32 ESP32 ESP-32S Development Board 2.4GHz Dual-Mode WiFi + Bluetooth Dual Cores Microcontroller The ESP32 integrated with Antenna switches, RF Balun, power amplifiers, low-noise amplifiers, filters, and management modules, and the entire solution occupies the least area of PCB. 2.4 GHz Wi-Fi plus Bluetooth dual-mode chip, with TSMC Ultra-low power consumption 40nm technology,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
