# Fritzing sketch schematics (saved by Fritzing 0.9.4)
breadboards: 1

parts:
  Part2 = Arduino Nano (Rev3.0) (ICSP)
  Disp1 = LBT2088AH [part_number=LBT2088AH]  # not connected

nets:
  N1: Part2.RESET, Part2.D10

notes:
  VCC
  GND
  DIN
  CS
  CLK
